# Fritzing sketch traffic-lights-01 (saved by Fritzing 0.9.3b)

parts:
  U1 = Explorer HAT Pro [part_number="Explorer HAT Pro" package=THT]
  LED1 = LED - 5mm [color="Red (633nm)" package="5 mm [THT]"]  # not connected
  R1 = Resistor [tolerance=±5% resistance=220 package=THT]  # not connected
  R2 = Resistor [tolerance=±5% resistance=220 package=THT]  # not connected
  R3 = Resistor [tolerance=±5% resistance=220 package=THT]  # not connected
  LED2 = LED - 5mm [color="Yellow (592nm)" package="5 mm [THT]"]  # not connected
  LED3 = LED - 5mm [color="Green (570nm)" package="5 mm [THT]"]  # not connected

nets:
  N1: U1.5v, U1.A5, U1.A7, U1.A9, U1.B5, U1.B7, U1.C5, U1.C7, U1.C9
  N2: U1.A6, U1.E6
  N3: U1.A8, U1.E8
  N4: U1.A10, U1.E10
  N5: U1.G6, U1.H6, U1.Output_1
  N6: U1.G8, U1.H8, U1.Output_2
  N7: U1.G10, U1.H10, U1.Output_3

custom parts:
  Explorer HAT Pro: Explorer HAT Pro with 4 Output and 4 Input connections, 4 Analog Inputs and 2 bi-directional motor channels, plus power and ground.
